// Logisim project IC CIRCUIT.circ as structural Verilog: 4 circuits, main circuit main
module main (
  input  A,
  input  B,
  input  C,
  output out_4
);

  wire and_ic_1_out_7, and_ic_1_out_8, and_ic_1_out_9, not_ic_1_out_4, not_ic_1_out_5, or_ic_1_out_7;

  NOT_IC not_ic_1 (.in_1(A), .in_2(B), .out_4(not_ic_1_out_4), .out_5(not_ic_1_out_5));  // open: in_3, out_6
  AND_IC and_ic_1 (
    .in_1(not_ic_1_out_4), .in_2(C), .in_3(A), .in_4(not_ic_1_out_5), .in_5(B), .in_6(C),
    .out_7(and_ic_1_out_7), .out_8(and_ic_1_out_8), .out_9(and_ic_1_out_9));
  OR_IC or_ic_1 (
    .in_1(and_ic_1_out_7), .in_2(and_ic_1_out_8), .in_3(or_ic_1_out_7), .in_4(and_ic_1_out_9),
    .out_7(or_ic_1_out_7), .out_8(out_4));  // open: in_5, in_6, out_9

  // Notes on the sheet:
  //   2
  //   1
  //   4
  //   3
  //   5
  //   6
  //   1
  //   3
  //   2
  //   4
  //   6
  //   5
  //   8
  //   9
  //   10
  //   1
  //   2
  //   3
  //   4
  //   5
  //   6
  //   9
  //   8
  //   10
endmodule

// AND
module AND_IC (
  input  in_1,
  input  in_2,
  input  in_3,
  input  in_4,
  input  in_5,
  input  in_6,
  output out_7,
  output out_8,
  output out_9
);

  and and_1 (out_7, in_1, in_2);
  and and_2 (out_8, in_3, in_4);
  and and_3 (out_9, in_5, in_6);
endmodule

// OR
module OR_IC (
  input  in_1,
  input  in_2,
  input  in_3,
  input  in_4,
  input  in_5,
  input  in_6,
  output out_7,
  output out_8,
  output out_9
);

  or or_1 (out_7, in_1, in_2);
  or or_2 (out_8, in_3, in_4);
  or or_3 (out_9, in_5, in_6);
endmodule

// NOT
module NOT_IC (
  input  in_1,
  input  in_2,
  input  in_3,
  output out_4,
  output out_5,
  output out_6
);

  not not_1 (out_4, in_1);
  not not_2 (out_5, in_2);
  not not_3 (out_6, in_3);
endmodule
