// Logisim project PIN OF LL GATES.circ as structural Verilog: 1 circuit, main circuit main
module main (
  input  in_1,
  input  in_2,
  input  in_3,
  input  in_4,
  input  in_5,
  input  in_6,
  input  in_7,
  input  in_8,
  input  in_9,
  input  in_10,
  input  in_11,
  output _2,
  output _3,
  output _3_2,
  output _3_3,
  output _1,
  output _3_4
);

  not not_1 (_2, in_1);
  and and_1 (_3, in_2, in_3);
  or or_1 (_3_2, in_4, in_5);
  nand nand_1 (_3_3, in_6, in_7);
  nor nor_1 (_1, in_8, in_9);
  xor xor_1 (_3_4, in_10, in_11);

  // Notes on the sheet:
  //   1
  //   1
  //   2
  //   1
  //   2
  //   1
  //   2
  //   2
  //   3
  //   1
  //   2
endmodule
