// Logisim project extended AND OR.circ as structural Verilog: 1 circuit, main circuit main
module main (
  input  _1,
  input  _2,
  input  in_3,
  input  _1_2,
  input  _2_2,
  input  in_6,
  output _6,
  output _6_2
);

  wire and_1_out, or_1_out;

  and and_1 (and_1_out, _1, _2);
  or or_1 (or_1_out, _1_2, _2_2);
  or or_2 (_6_2, or_1_out, in_6);
  and and_2 (_6, and_1_out, in_3);

  // Notes on the sheet:
  //   3
  //   3
  //   5
  //   4
  //   5
  //   4
endmodule
