// Logisim project TASK1+2 (NAND).circ as structural Verilog: 1 circuit, main circuit main
module main (
  input  in_1,
  input  in_2,
  output NOT_USING_NAND,
  output AND_USING_NAND,
  output OR_USING_NAND,
  output XOR_USING_NAND,
  output XNOR_USING_NAND
);

  wire nand_1_out, nand_2_out, nand_4_out, nand_5_out, nand_6_out, nand_7_out, nand_8_out, nand_11_out,
       nand_12_out, nand_14_out;

  nand nand_1 (nand_1_out, in_2, in_1);
  nand nand_2 (nand_2_out, in_2, in_1);
  nand nand_3 (NOT_USING_NAND, in_2, in_2);
  nand nand_4 (nand_4_out, in_2, in_1);
  nand nand_5 (nand_5_out, in_2, in_2);
  nand nand_6 (nand_6_out, in_1, in_1);
  nand nand_7 (nand_7_out, in_2, nand_2_out);
  nand nand_8 (nand_8_out, nand_2_out, in_1);
  nand nand_9 (AND_USING_NAND, nand_4_out, nand_4_out);
  nand nand_10 (OR_USING_NAND, nand_5_out, nand_6_out);
  nand nand_11 (nand_11_out, in_2, nand_1_out);
  nand nand_12 (nand_12_out, nand_1_out, in_1);
  nand nand_13 (XOR_USING_NAND, nand_11_out, nand_12_out);
  nand nand_14 (nand_14_out, nand_7_out, nand_8_out);
  nand nand_15 (XNOR_USING_NAND, nand_14_out, nand_14_out);
endmodule
