// Logisim project TASK1+2 (NOR).circ as structural Verilog: 1 circuit, main circuit main
module main (
  input  in_1,
  input  in_2,
  output NOT_USING_NOR,
  output AND_USING_NOR,
  output OR_USING_NOR,
  output XOR_USING_NOR,
  output XNOR_USING_NOR
);

  wire nor_2_out, nor_3_out, nor_4_out, nor_5_out, nor_6_out, nor_7_out, nor_8_out, nor_11_out, nor_12_out,
       nor_13_out;

  nor nor_1 (NOT_USING_NOR, in_2, in_2);
  nor nor_2 (nor_2_out, in_2, in_2);
  nor nor_3 (nor_3_out, in_1, in_1);
  nor nor_4 (nor_4_out, in_2, in_1);
  nor nor_5 (nor_5_out, in_2, in_2);
  nor nor_6 (nor_6_out, in_1, in_1);
  nor nor_7 (nor_7_out, in_2, in_1);
  nor nor_8 (nor_8_out, in_2, in_1);
  nor nor_9 (AND_USING_NOR, nor_2_out, nor_3_out);
  nor nor_10 (OR_USING_NOR, nor_4_out, nor_4_out);
  nor nor_11 (nor_11_out, nor_5_out, nor_6_out);
  nor nor_12 (nor_12_out, in_2, nor_8_out);
  nor nor_13 (nor_13_out, nor_8_out, in_1);
  nor nor_14 (XOR_USING_NOR, nor_11_out, nor_7_out);
  nor nor_15 (XNOR_USING_NOR, nor_12_out, nor_13_out);
endmodule
