// Logisim project TASK3 USING NAND.circ as structural Verilog: 5 circuits, main circuit main
module main (
  input  A,
  input  B,
  input  C,
  output out_4
);

  wire nand_ic_1_out_9, nand_ic_1_out_10, nand_ic_1_out_11;

  nand_ic nand_ic_1 (
    .in_1(C), .in_2(A), .in_3(C), .in_4(C), .in_5(nand_ic_1_out_10), .in_6(B), .in_7(nand_ic_1_out_11),
    .in_8(nand_ic_1_out_9), .out_9(nand_ic_1_out_9), .out_10(nand_ic_1_out_10), .out_11(nand_ic_1_out_11),
    .out_12(out_4));
endmodule

// A N D
module AND_IC (
  input  in_1,
  input  in_2,
  input  in_3,
  input  in_4,
  output out_5,
  output out_6
);

  wire nand_1_out, nand_2_out;

  nand nand_1 (nand_1_out, in_1, in_2);
  nand nand_2 (nand_2_out, in_3, in_4);
  nand nand_3 (out_5, nand_1_out, nand_1_out);
  nand nand_4 (out_6, nand_2_out, nand_2_out);
endmodule

// O R
module OR_IC (
  input  in_1,
  input  in_2,
  input  in_3,
  input  in_4,
  output out_5,
  output out_6
);

  wire nand_1_out, nand_2_out, nand_3_out, nand_4_out;

  nand nand_1 (nand_1_out, in_1, in_1);
  nand nand_2 (nand_2_out, in_2, in_2);
  nand nand_3 (nand_3_out, in_3, in_3);
  nand nand_4 (nand_4_out, in_4, in_4);
  nand nand_5 (out_5, nand_1_out, nand_2_out);
  nand nand_6 (out_6, nand_3_out, nand_4_out);
endmodule

// N O T
module NOT_IC (
  input  in_1,
  input  in_2,
  output out_3,
  output out_4
);

  nand nand_1 (out_3, in_1, in_1);
  nand nand_2 (out_4, in_2, in_2);
endmodule

module nand_ic (
  input  in_1,
  input  in_2,
  input  in_3,
  input  in_4,
  input  in_5,
  input  in_6,
  input  in_7,
  input  in_8,
  output out_9,
  output out_10,
  output out_11,
  output out_12
);

  nand nand_1 (out_9, in_1, in_2);
  nand nand_2 (out_10, in_3, in_4);
  nand nand_3 (out_11, in_5, in_6);
  nand nand_4 (out_12, in_7, in_8);
endmodule
