// Logisim project TASK3 USING NOR.circ as structural Verilog: 5 circuits, main circuit main
module main (
  input  A,
  input  B,
  input  C,
  output out_4
);

  wire nor_ic_1_out_9, nor_ic_1_out_10, nor_ic_1_out_11, nor_ic_1_out_12, nor_ic_2_out_9, nor_ic_2_out_10;

  NOR_IC nor_ic_1 (
    .in_1(C), .in_2(C), .in_3(A), .in_4(A), .in_5(B), .in_6(B), .in_7(nor_ic_1_out_10),
    .in_8(nor_ic_1_out_9), .out_9(nor_ic_1_out_9), .out_10(nor_ic_1_out_10), .out_11(nor_ic_1_out_11),
    .out_12(nor_ic_1_out_12));
  NOR_IC nor_ic_2 (
    .in_1(nor_ic_1_out_12), .in_2(nor_ic_2_out_10), .in_3(nor_ic_1_out_11), .in_4(C), .in_5(nor_ic_2_out_9),
    .in_6(nor_ic_2_out_9), .out_9(nor_ic_2_out_9), .out_10(nor_ic_2_out_10), .out_11(out_4));  // open: in_7, in_8, out_12
endmodule

// AND
module AND_IC (
  input  in_1,
  input  in_2,
  input  in_3,
  input  in_4,
  output out_5,
  output out_6
);

  wire nor_1_out, nor_2_out, nor_3_out, nor_4_out;

  nor nor_1 (nor_1_out, in_1, in_1);
  nor nor_2 (nor_2_out, in_2, in_2);
  nor nor_3 (nor_3_out, in_3, in_3);
  nor nor_4 (nor_4_out, in_4, in_4);
  nor nor_5 (out_5, nor_1_out, nor_2_out);
  nor nor_6 (out_6, nor_3_out, nor_4_out);
endmodule

// OR
module OR_IC (
  input  in_1,
  input  in_2,
  output out_3
);

  wire nor_1_out;

  nor nor_1 (nor_1_out, in_1, in_2);
  nor nor_2 (out_3, nor_1_out, nor_1_out);
endmodule

// NOT
module NOT_IC (
  input  in_1,
  output out_2
);

  nor nor_1 (out_2, in_1, in_1);
endmodule

module NOR_IC (
  input  in_1,
  input  in_2,
  input  in_3,
  input  in_4,
  input  in_5,
  input  in_6,
  input  in_7,
  input  in_8,
  output out_9,
  output out_10,
  output out_11,
  output out_12
);

  nor nor_1 (out_9, in_1, in_2);
  nor nor_2 (out_10, in_3, in_4);
  nor nor_3 (out_11, in_5, in_6);
  nor nor_4 (out_12, in_7, in_8);
endmodule
