// Logisim project MAX TERM.circ as structural Verilog: 4 circuits, main circuit main
module main (
  input  A,
  input  B,
  input  C,
  output out_4
);

  wire n3_input_and_gate_1_out_10, n3_input_or_gate_1_out_10, n3_input_or_gate_1_out_11,
       n3_input_or_gate_1_out_12, n3_input_or_gate_2_out_10, n3_input_or_gate_2_out_11, not_gate_1_out_7,
       not_gate_1_out_8, not_gate_1_out_9;

  NOT_gate not_gate_1 (
    .in_1(A), .out_7(not_gate_1_out_7), .in_2(B), .out_8(not_gate_1_out_8), .in_3(C), .out_9(not_gate_1_out_9));  // open: in_4, out_10, in_5, out_11, in_6, out_12
  _3_input_OR_gate u_3_input_or_gate_1 (
    .in_1(A), .in_2(B), .in_3(C), .in_4(not_gate_1_out_7), .in_5(not_gate_1_out_8), .in_6(not_gate_1_out_9),
    .in_7(A), .in_8(not_gate_1_out_8), .in_9(not_gate_1_out_9), .out_10(n3_input_or_gate_1_out_10),
    .out_11(n3_input_or_gate_1_out_11), .out_12(n3_input_or_gate_1_out_12));
  _3_input_OR_gate u_3_input_or_gate_2 (
    .in_1(not_gate_1_out_7), .in_2(B), .in_3(C), .in_4(not_gate_1_out_7), .in_5(B), .in_6(not_gate_1_out_9),
    .out_10(n3_input_or_gate_2_out_10), .out_11(n3_input_or_gate_2_out_11));  // open: in_7, in_8, in_9, out_12
  _3_input_AND_gate u_3_input_and_gate_1 (
    .in_1(n3_input_or_gate_1_out_10), .in_2(n3_input_or_gate_1_out_11), .in_3(n3_input_or_gate_1_out_12),
    .in_4(n3_input_and_gate_1_out_10), .in_5(n3_input_or_gate_2_out_10), .in_6(n3_input_or_gate_2_out_11),
    .out_10(n3_input_and_gate_1_out_10), .out_11(out_4));  // open: in_7, in_8, in_9, out_12
endmodule

// 3-input AND
module _3_input_AND_gate (
  input  in_1,
  input  in_2,
  input  in_3,
  input  in_4,
  input  in_5,
  input  in_6,
  input  in_7,
  input  in_8,
  input  in_9,
  output out_10,
  output out_11,
  output out_12
);

  and and_1 (out_10, in_1, in_2, in_3);
  and and_2 (out_11, in_4, in_5, in_6);
  and and_3 (out_12, in_7, in_8, in_9);
endmodule

// 3-input OR
module _3_input_OR_gate (
  input  in_1,
  input  in_2,
  input  in_3,
  input  in_4,
  input  in_5,
  input  in_6,
  input  in_7,
  input  in_8,
  input  in_9,
  output out_10,
  output out_11,
  output out_12
);

  or or_1 (out_10, in_1, in_2, in_3);
  or or_2 (out_11, in_4, in_5, in_6);
  or or_3 (out_12, in_7, in_8, in_9);
endmodule

// NOT
module NOT_gate (
  input  in_1,
  input  in_2,
  input  in_3,
  input  in_4,
  input  in_5,
  input  in_6,
  output out_7,
  output out_8,
  output out_9,
  output out_10,
  output out_11,
  output out_12
);

  not not_1 (out_7, in_1);
  not not_2 (out_8, in_2);
  not not_3 (out_9, in_3);
  not not_4 (out_10, in_4);
  not not_5 (out_11, in_5);
  not not_6 (out_12, in_6);
endmodule
