// Logisim project IC CIRCUIT.circ as structural Verilog: 4 circuits, main circuit main
module main (
  input  W,
  input  X,
  input  Y,
  input  Z,
  output out_5,
  output out_6,
  output out_7,
  output out_8
);

  wire and_ic_1_out_9, and_ic_1_out_10, and_ic_1_out_11, and_ic_1_out_12, and_ic_2_out_9, and_ic_2_out_10,
       and_ic_2_out_11, and_ic_2_out_12, not_ic_1_out_5, not_ic_1_out_6, or_ic_1_out_9, or_ic_1_out_11;

  NOT_IC not_ic_1 (
    .in_1(X), .in_2(Y), .in_3(Z), .out_5(not_ic_1_out_5), .out_6(not_ic_1_out_6), .out_7(out_8));  // open: in_4, out_8
  AND_IC and_ic_1 (
    .in_1(X), .in_2(Z), .in_3(X), .in_4(Y), .in_5(not_ic_1_out_5), .in_6(Z), .out_9(and_ic_1_out_9),
    .out_10(and_ic_1_out_10), .out_11(and_ic_1_out_11), .in_7(not_ic_1_out_5), .out_12(and_ic_1_out_12),
    .in_8(Y));
  AND_IC and_ic_2 (
    .in_1(X), .in_2(not_ic_1_out_6), .in_3(and_ic_2_out_9), .in_4(out_8), .in_5(Y), .in_6(Z),
    .out_9(and_ic_2_out_9), .out_10(and_ic_2_out_10), .out_11(and_ic_2_out_11), .in_7(not_ic_1_out_6),
    .out_12(and_ic_2_out_12), .in_8(out_8));
  OR_IC or_ic_1 (
    .in_1(W), .in_2(and_ic_1_out_9), .in_3(and_ic_1_out_10), .in_4(or_ic_1_out_9), .in_5(and_ic_1_out_11),
    .in_6(and_ic_1_out_12), .out_9(or_ic_1_out_9), .out_10(out_5), .out_11(or_ic_1_out_11),
    .in_7(or_ic_1_out_11), .out_12(out_6), .in_8(and_ic_2_out_10));
  OR_IC or_ic_2 (
    .in_1(and_ic_2_out_11), .in_2(and_ic_2_out_12), .out_9(out_7));  // open: in_3, in_4, in_5, in_6, out_10, out_11, in_7, out_12, in_8
endmodule

// AND
module AND_IC (
  input  in_1,
  input  in_2,
  input  in_3,
  input  in_4,
  input  in_5,
  input  in_6,
  input  in_7,
  input  in_8,
  output out_9,
  output out_10,
  output out_11,
  output out_12
);

  and and_1 (out_9, in_1, in_2);
  and and_2 (out_10, in_3, in_4);
  and and_3 (out_11, in_5, in_6);
  and and_4 (out_12, in_7, in_8);
endmodule

// OR
module OR_IC (
  input  in_1,
  input  in_2,
  input  in_3,
  input  in_4,
  input  in_5,
  input  in_6,
  input  in_7,
  input  in_8,
  output out_9,
  output out_10,
  output out_11,
  output out_12
);

  or or_1 (out_9, in_1, in_2);
  or or_2 (out_10, in_3, in_4);
  or or_3 (out_11, in_5, in_6);
  or or_4 (out_12, in_7, in_8);
endmodule

// NOT
module NOT_IC (
  input  in_1,
  input  in_2,
  input  in_3,
  input  in_4,
  output out_5,
  output out_6,
  output out_7,
  output out_8
);

  not not_1 (out_5, in_1);
  not not_2 (out_6, in_2);
  not not_3 (out_7, in_3);
  not not_4 (out_8, in_4);
endmodule
