// Logisim project 4bit Adder .circ as structural Verilog: 3 circuits, main circuit main
module main (
  input  [3:0] B,
  input  [3:0] A,
  input  [3:0] B_2,
  input  [3:0] A_2,
  output out_5,
  output [3:0] out_6,
  output out_7,
  output [3:0] out_8
);

  ADDER_IC adder_ic_1 (
    .A1(A[0]), .B1(B[0]), .Cin(1'b0), .A2(A[1]), .B2(B[1]), .A3(A[2]), .B3(B[2]), .A4(A[3]), .B4(B[3]),
    .out_10(out_6[0]), .out_11(out_6[1]), .out_12(out_6[2]), .out_13(out_6[3]), .out_14(out_5));
  _4_BIT_LOGISM_ADDER u_4_bit_logism_adder_1 (
    .Cin(1'b0), .A1(A_2[0]), .B1(B_2[0]), .A2(A_2[1]), .B2(B_2[1]), .A3(A_2[2]), .B3(B_2[2]), .A4(A_2[3]),
    .B4(B_2[3]), .out_10(out_8[0]), .out_11(out_8[1]), .out_12(out_8[2]), .out_13(out_8[3]), .out_14(out_7));

  // Notes on the sheet:
  //   FIG:4-BIT ADDER using basic gates
  //   FIG:4-BIT ADDER
endmodule

// 4 BIT ADDER IC
module ADDER_IC (
  input  A1,
  input  B1,
  input  Cin,
  input  A2,
  input  B2,
  input  A3,
  input  B3,
  input  A4,
  input  B4,
  output out_10,
  output out_11,
  output out_12,
  output out_13,
  output out_14
);

  wire and_1_out, and_2_out, and_3_out, and_4_out, and_5_out, and_6_out, and_7_out, and_8_out, or_1_out,
       or_2_out, or_3_out, xor_1_out, xor_2_out, xor_3_out, xor_4_out;

  xor xor_1 (xor_1_out, A1, B1);
  and and_1 (and_1_out, A1, B1);
  xor xor_2 (xor_2_out, A2, B2);
  and and_2 (and_2_out, A2, B2);
  xor xor_3 (xor_3_out, A3, B3);
  and and_3 (and_3_out, A3, B3);
  xor xor_4 (xor_4_out, A4, B4);
  and and_4 (and_4_out, A4, B4);
  xor xor_5 (out_10, xor_1_out, Cin);
  and and_5 (and_5_out, xor_1_out, Cin);
  and and_6 (and_6_out, xor_2_out, or_1_out);
  and and_7 (and_7_out, xor_3_out, or_2_out);
  and and_8 (and_8_out, xor_4_out, or_3_out);
  xor xor_6 (out_11, xor_2_out, or_1_out);
  xor xor_7 (out_12, xor_3_out, or_2_out);
  xor xor_8 (out_13, xor_4_out, or_3_out);
  or or_1 (or_1_out, and_5_out, and_1_out);
  or or_2 (or_2_out, and_6_out, and_2_out);
  or or_3 (or_3_out, and_7_out, and_3_out);
  or or_4 (out_14, and_8_out, and_4_out);
endmodule

// ADDER
module _4_BIT_LOGISM_ADDER (
  input  Cin,
  input  A1,
  input  B1,
  input  A2,
  input  B2,
  input  A3,
  input  B3,
  input  A4,
  input  B4,
  output out_10,
  output out_11,
  output out_12,
  output out_13,
  output out_14
);

  wire adder_1_cout, adder_2_cout, adder_3_cout;

  Adder #(.width(1)) adder_1 (.a(A1), .b(B1), .out(out_10), .cin(Cin), .cout(adder_1_cout));
  Adder #(.width(1)) adder_2 (.a(A2), .b(B2), .out(out_11), .cin(adder_1_cout), .cout(adder_2_cout));
  Adder #(.width(1)) adder_3 (.a(A3), .b(B3), .out(out_12), .cin(adder_2_cout), .cout(adder_3_cout));
  Adder #(.width(1)) adder_4 (.a(A4), .b(B4), .out(out_13), .cin(adder_3_cout), .cout(out_14));
endmodule
