// Logisim project 4bit Adder-Subtractor.circ as structural Verilog: 4 circuits, main circuit main
module main (
  input  [3:0] B,
  input  [3:0] A,
  input  Cin,
  input  [3:0] B_2,
  input  [3:0] A_2,
  input  Cin_2,
  output out_7,
  output [3:0] out_8,
  output out_9,
  output [3:0] out_10
);

  wire xor_ic_1_out_9, xor_ic_1_out_10, xor_ic_1_out_11, xor_ic_1_out_12, xor_ic_2_out_9, xor_ic_2_out_10,
       xor_ic_2_out_11, xor_ic_2_out_12;

  XOR_IC xor_ic_1 (
    .in_1(B[0]), .in_2(Cin), .in_3(B[1]), .in_4(Cin), .in_5(B[2]), .in_6(Cin), .in_7(B[3]), .in_8(Cin),
    .out_9(xor_ic_1_out_9), .out_10(xor_ic_1_out_10), .out_11(xor_ic_1_out_11), .out_12(xor_ic_1_out_12));
  XOR_IC xor_ic_2 (
    .in_1(B_2[0]), .in_2(Cin_2), .in_3(B_2[1]), .in_4(Cin_2), .in_5(B_2[2]), .in_6(Cin_2), .in_7(B_2[3]),
    .in_8(Cin_2), .out_9(xor_ic_2_out_9), .out_10(xor_ic_2_out_10), .out_11(xor_ic_2_out_11),
    .out_12(xor_ic_2_out_12));
  ADDER_IC adder_ic_1 (
    .A1(A[0]), .B1(xor_ic_1_out_9), .Cin(Cin), .A2(A[1]), .B2(xor_ic_1_out_10), .A3(A[2]),
    .B3(xor_ic_1_out_11), .A4(A[3]), .B4(xor_ic_1_out_12), .out_10(out_8[0]), .out_11(out_8[1]),
    .out_12(out_8[2]), .out_13(out_8[3]), .out_14(out_7));
  _4_bit_Logism_ADDER u_4_bit_logism_adder_1 (
    .in_1(Cin_2), .in_2(A_2[0]), .in_3(xor_ic_2_out_9), .in_4(A_2[1]), .in_5(xor_ic_2_out_10), .in_6(A_2[2]),
    .in_7(xor_ic_2_out_11), .in_8(A_2[3]), .in_9(xor_ic_2_out_12), .out_10(out_10[0]), .out_11(out_10[1]),
    .out_12(out_10[2]), .out_13(out_10[3]), .out_14(out_9));

  // Notes on the sheet:
  //   FIG:4-BIT ADDER SUBTRACTOR using basic gates
  //   FIG:4-BIT ADDER SUBTRACTOR 
endmodule

module XOR_IC (
  input  in_1,
  input  in_2,
  input  in_3,
  input  in_4,
  input  in_5,
  input  in_6,
  input  in_7,
  input  in_8,
  output out_9,
  output out_10,
  output out_11,
  output out_12
);

  xor xor_1 (out_9, in_1, in_2);
  xor xor_2 (out_10, in_3, in_4);
  xor xor_3 (out_11, in_5, in_6);
  xor xor_4 (out_12, in_7, in_8);
endmodule

// 4 BIT ADDER IC
module ADDER_IC (
  input  A1,
  input  B1,
  input  Cin,
  input  A2,
  input  B2,
  input  A3,
  input  B3,
  input  A4,
  input  B4,
  output out_10,
  output out_11,
  output out_12,
  output out_13,
  output out_14
);

  wire and_1_out, and_2_out, and_3_out, and_4_out, and_5_out, and_6_out, and_7_out, and_8_out, or_1_out,
       or_2_out, or_3_out, xor_1_out, xor_2_out, xor_3_out, xor_4_out;

  xor xor_1 (xor_1_out, A1, B1);
  and and_1 (and_1_out, B1, B1);
  xor xor_2 (xor_2_out, A2, B2);
  and and_2 (and_2_out, B2, B2);
  xor xor_3 (xor_3_out, A3, B3);
  and and_3 (and_3_out, B3, B3);
  xor xor_4 (xor_4_out, A4, B4);
  and and_4 (and_4_out, B4, B4);
  xor xor_5 (out_10, xor_1_out, Cin);
  and and_5 (and_5_out, xor_1_out, Cin);
  and and_6 (and_6_out, xor_2_out, or_1_out);
  and and_7 (and_7_out, xor_3_out, or_2_out);
  and and_8 (and_8_out, xor_4_out, or_3_out);
  xor xor_6 (out_11, xor_2_out, or_1_out);
  xor xor_7 (out_12, xor_3_out, or_2_out);
  xor xor_8 (out_13, xor_4_out, or_3_out);
  or or_1 (or_1_out, and_5_out, and_1_out);
  or or_2 (or_2_out, and_6_out, and_2_out);
  or or_3 (or_3_out, and_7_out, and_3_out);
  or or_4 (out_14, and_8_out, and_4_out);
endmodule

// LOGISM ADDER
module _4_bit_Logism_ADDER (
  input  in_1,
  input  in_2,
  input  in_3,
  input  in_4,
  input  in_5,
  input  in_6,
  input  in_7,
  input  in_8,
  input  in_9,
  output out_10,
  output out_11,
  output out_12,
  output out_13,
  output out_14
);

  wire adder_1_cout, adder_2_cout, adder_3_cout;

  Adder #(.width(1)) adder_1 (.a(in_2), .b(in_3), .out(out_10), .cin(in_1), .cout(adder_1_cout));
  Adder #(.width(1)) adder_2 (.a(in_4), .b(in_5), .out(out_11), .cin(adder_1_cout), .cout(adder_2_cout));
  Adder #(.width(1)) adder_3 (.a(in_6), .b(in_7), .out(out_12), .cin(adder_2_cout), .cout(adder_3_cout));
  Adder #(.width(1)) adder_4 (.a(in_8), .b(in_9), .out(out_13), .cin(adder_3_cout), .cout(out_14));
endmodule
