// Logisim project BCD ADDER.circ as structural Verilog: 4 circuits, main circuit main
module main (
  input  [3:0] B,
  input  [3:0] A,
  input  Cin,
  output BCD_Carry,
  output COUT,
  output [3:0] out_6
);

  wire and_ic_1_out_9, and_ic_1_out_10, n4_bit_logism_adder_1_out_10, n4_bit_logism_adder_1_out_11,
       n4_bit_logism_adder_1_out_12, n4_bit_logism_adder_1_out_13, n4_bit_logism_adder_1_out_14,
       or_ic_1_out_9;

  _4_bit_Logism_ADDER u_4_bit_logism_adder_1 (
    .in_1(Cin), .in_2(A[0]), .in_3(B[0]), .in_4(A[1]), .in_5(B[1]), .in_6(A[2]), .in_7(B[2]), .in_8(A[3]),
    .in_9(B[3]), .out_10(n4_bit_logism_adder_1_out_10), .out_11(n4_bit_logism_adder_1_out_11),
    .out_12(n4_bit_logism_adder_1_out_12), .out_13(n4_bit_logism_adder_1_out_13),
    .out_14(n4_bit_logism_adder_1_out_14));
  _4_bit_Logism_ADDER u_4_bit_logism_adder_2 (
    .in_2(n4_bit_logism_adder_1_out_10), .in_3(1'b0), .in_4(n4_bit_logism_adder_1_out_11), .in_5(BCD_Carry),
    .in_6(n4_bit_logism_adder_1_out_12), .in_7(BCD_Carry), .in_8(n4_bit_logism_adder_1_out_13), .in_9(1'b0),
    .out_10(out_6[0]), .out_11(out_6[1]), .out_12(out_6[2]), .out_13(out_6[3]), .out_14(COUT));  // open: in_1
  AND_IC and_ic_1 (
    .in_1(n4_bit_logism_adder_1_out_13), .in_2(n4_bit_logism_adder_1_out_12),
    .in_3(n4_bit_logism_adder_1_out_11), .in_4(n4_bit_logism_adder_1_out_13), .out_9(and_ic_1_out_9),
    .out_10(and_ic_1_out_10));  // open: in_5, in_6, out_11, in_7, out_12, in_8
  OR_IC or_ic_1 (
    .in_1(and_ic_1_out_9), .in_2(and_ic_1_out_10), .out_9(or_ic_1_out_9),
    .in_3(n4_bit_logism_adder_1_out_14), .out_10(BCD_Carry), .in_4(or_ic_1_out_9));  // open: in_5, out_11, in_6, in_7, out_12, in_8

  // Notes on the sheet:
  //   FIG:BCD ADDER
endmodule

// AND
module AND_IC (
  input  in_1,
  input  in_2,
  input  in_3,
  input  in_4,
  input  in_5,
  input  in_6,
  input  in_7,
  input  in_8,
  output out_9,
  output out_10,
  output out_11,
  output out_12
);

  and and_1 (out_9, in_1, in_2);
  and and_2 (out_10, in_3, in_4);
  and and_3 (out_11, in_5, in_6);
  and and_4 (out_12, in_7, in_8);
endmodule

// OR
module OR_IC (
  input  in_1,
  input  in_2,
  input  in_3,
  input  in_4,
  input  in_5,
  input  in_6,
  input  in_7,
  input  in_8,
  output out_9,
  output out_10,
  output out_11,
  output out_12
);

  or or_1 (out_9, in_1, in_2);
  or or_2 (out_10, in_3, in_4);
  or or_3 (out_11, in_5, in_6);
  or or_4 (out_12, in_7, in_8);
endmodule

// LOGISM ADDER
module _4_bit_Logism_ADDER (
  input  in_1,
  input  in_2,
  input  in_3,
  input  in_4,
  input  in_5,
  input  in_6,
  input  in_7,
  input  in_8,
  input  in_9,
  output out_10,
  output out_11,
  output out_12,
  output out_13,
  output out_14
);

  wire adder_1_cout, adder_2_cout, adder_3_cout;

  Adder #(.width(1)) adder_1 (.a(in_2), .b(in_3), .out(out_10), .cin(in_1), .cout(adder_1_cout));
  Adder #(.width(1)) adder_2 (.a(in_4), .b(in_5), .out(out_11), .cin(adder_1_cout), .cout(adder_2_cout));
  Adder #(.width(1)) adder_3 (.a(in_6), .b(in_7), .out(out_12), .cin(adder_2_cout), .cout(adder_3_cout));
  Adder #(.width(1)) adder_4 (.a(in_8), .b(in_9), .out(out_13), .cin(adder_3_cout), .cout(out_14));
endmodule
