// Logisim project MUX ALL FILE IN ONE.circ as structural Verilog: 2 circuits, main circuit main
module main (
  input  enable,
  input  I0,
  input  I1,
  input  I2,
  input  I3,
  input  S1,
  input  S0,
  output out_8
);

  wire and_1_out, and_2_out, and_3_out, and_4_out, not_1_out, not_2_out, or_1_out, or_2_out;

  not not_1 (not_1_out, S1);
  not not_2 (not_2_out, S0);
  and and_1 (and_1_out, I0, not_1_out, not_2_out, enable);
  and and_2 (and_2_out, I1, not_1_out, S0, enable);
  and and_3 (and_3_out, I2, S1, not_2_out, enable);
  and and_4 (and_4_out, I3, S0, S1, enable);
  or or_1 (or_1_out, and_1_out, and_2_out);
  or or_2 (or_2_out, and_3_out, and_4_out);
  or or_3 (out_8, or_1_out, or_2_out);

  // Notes on the sheet:
  //   FIG:     4:1 MULTIPLEXER USING BASIC LOGIC GATES
endmodule

module MULTIPLEXER_8_1 (
  input  D,
  input  [2:0] ABC,
  output out_3
);

  Multiplexer #(.select(3)) multiplexer_1 (
    .in0(1'b1), .in1(D), .in2(D), .in3(1'b0), .in4(1'b1), .in5(1'b0), .in6(1'b0), .in7(1'b1), .out(out_3),
    .sel(ABC));  // open: en

  // Notes on the sheet:
  //   FIG:   8:1 MULTIPLEXER FROM TABE F.2.1
endmodule
