// Logisim project FlipFlop.circ as structural Verilog: 1 circuit, main circuit main
module main (
  input  in_1,
  output DA,
  output DB
);

  wire clock_1_out, d_ff_2_qn, xor_1_out, xor_2_out;

  xor xor_1 (xor_1_out, DA, DB);
  xor xor_2 (xor_2_out, xor_1_out, in_1);
  Clock clock_1 (.out(clock_1_out));
  D_Flip_Flop d_ff_1 (.clk(clock_1_out), .D(xor_2_out), .Q(DA));  // open: Qn, preset, en, reset
  D_Flip_Flop d_ff_2 (.clk(clock_1_out), .D(d_ff_2_qn), .Q(DB), .Qn(d_ff_2_qn));  // open: preset, en, reset

  // Notes on the sheet:
  //   A
  //   B
endmodule
